// Logisim project CT8.circ as structural Verilog
module ALU (
  input  CEnbl,
  input  Cin,
  input  OutEn,
  input  [7:0] A,
  input  [7:0] B,
  input  [5:0] in_6,
  output SF,
  output [7:0] Dout,
  output COut
);

  wire and_1_out, or_2_out, xor_2_out;
  wire [7:0] adder_1_out, and_2_out, controlled_buffer_1_out, not_1_out, or_1_out, xor_1_out, xor_3_out;

  // Probe on A
  // Probe on B
  assign xor_1_out = B ^ {8{in_6[1]}};  // XOR_Gate xor_1, 8 bits wide
  and and_1 (and_1_out, CEnbl, Cin);
  xor xor_2 (xor_2_out, and_1_out, in_6[1]);
  Adder adder_1 (.a(A), .b(xor_1_out), .out(adder_1_out), .cin(xor_2_out), .cout(COut));
  assign and_2_out = A & xor_1_out;  // AND_Gate and_2, 8 bits wide
  assign or_1_out = A | xor_1_out;  // OR_Gate or_1, 8 bits wide
  assign xor_3_out = A ^ xor_1_out;  // XOR_Gate xor_3, 8 bits wide
  assign not_1_out = ~xor_1_out;  // NOT_Gate not_1, 8 bits wide
  or or_2 (or_2_out, in_6[1], in_6[0]);
  assign controlled_buffer_1_out = or_2_out ? adder_1_out : 8'bz;  // Controlled_Buffer controlled_buffer_1
  assign controlled_buffer_1_out = in_6[2] ? and_2_out : 8'bz;  // Controlled_Buffer controlled_buffer_2
  assign controlled_buffer_1_out = in_6[3] ? or_1_out : 8'bz;  // Controlled_Buffer controlled_buffer_3
  assign controlled_buffer_1_out = in_6[4] ? xor_3_out : 8'bz;  // Controlled_Buffer controlled_buffer_4
  assign controlled_buffer_1_out = in_6[5] ? not_1_out : 8'bz;  // Controlled_Buffer controlled_buffer_5
  // Probe on Dout
  assign Dout = OutEn ? controlled_buffer_1_out : 8'bz;  // Controlled_Buffer controlled_buffer_6

  assign SF = OutEn;
endmodule

module instrDecoder (
  input  [7:0] instr,
  output ADD_op,
  output HLT,
  output SUB_op,
  output AND_op,
  output CMP_op,
  output OR_op,
  output ALUop,
  output XOR_op,
  output NOT_op,
  output LW,
  output SW,
  output MOV,
  output JMP,
  output JZ,
  output JC,
  output NOP,
  output HLuse,
  output [2:0] REG_MUX,
  output MemRegOp
);

  wire and_3_out, demultiplexer_2_out1, demultiplexer_2_out7, nor_1_out, or_1_out, or_2_out, or_4_out;

  and and_1 (HLT, instr[0], instr[1], instr[2], instr[3]);
  and and_2 (ALUop, ~HLT, instr[3]);  // AND_Gate
  nor nor_1 (nor_1_out, HLT, instr[3]);
  Demultiplexer #(.select(3)) demultiplexer_1 (
    .out1(LW), .out2(SW), .out3(MOV), .out4(JMP), .out5(JZ), .out6(JC), .out7(NOP), .in(nor_1_out),
    .sel(instr[2:0]));  // open: out0
  and and_3 (and_3_out, ~or_2_out, instr[4]);  // AND_Gate
  assign REG_MUX = and_3_out ? instr[7:5] : 3'bz;  // Controlled_Buffer controlled_buffer_1
  and and_4 (MemRegOp, instr[4], ~HLT, ~NOP);  // AND_Gate
  Demultiplexer #(.select(3)) demultiplexer_2 (
    .out0(ADD_op), .out1(demultiplexer_2_out1), .out2(AND_op), .out3(OR_op), .out4(XOR_op), .out5(NOT_op),
    .out6(CMP_op), .out7(demultiplexer_2_out7), .in(ALUop), .sel(instr[2:0]));
  or or_1 (or_1_out, SW, LW);
  or or_2 (or_2_out, JMP, JZ, JC);
  or or_3 (SUB_op, demultiplexer_2_out1, CMP_op);
  or or_4 (or_4_out, or_1_out, or_2_out);
  and and_5 (HLuse, or_4_out, MemRegOp);

  // Notes on the sheet:
  //   regImportant
  //   NoREG
endmodule

module regs (
  input  [7:0] Din,
  input  WE,
  input  Clck,
  input  Rst,
  input  OE,
  output [7:0] Dout
);

  wire [7:0] register_1_q;

  Register register_1 (.D(Din), .en(WE), .clk(Clck), .Q(register_1_q), .clr(Rst));
  assign Dout = OE ? register_1_q : 8'bz;  // Controlled_Buffer controlled_buffer_1
endmodule

module instrReg (
  input  [7:0] instIn,
  input  WE,
  input  Clck,
  input  Rst,
  output [7:0] out_5
);

  Register register_1 (.D(instIn), .en(WE), .clk(Clck), .Q(out_5), .clr(Rst));
endmodule

module flagReg (
  input  [7:0] Din,
  input  Carryin,
  input  WE,
  input  Clck,
  input  Rst,
  output [3:0] Dout,
  output Cout
);

  wire [3:3] and_1_out;

  and and_1 (and_1_out[3], ~Din[0], ~Din[1], ~Din[2], ~Din[3], ~Din[4], ~Din[5], ~Din[6], ~Din[7]);  // AND_Gate
  Register #(.width(4)) register_1 (
    .D({and_1_out[3], Din[0], Din[7], Carryin}), .en(WE), .clk(Clck), .Q({Dout[3:1], Cout}), .clr(Rst));

  assign Dout[0] = Cout;

  // Notes on the sheet:
  //   odd
  //   N
  //   Z
endmodule

module RegBank (
  input  [7:0] Datain,
  input  OE,
  input  Clk,
  input  reset,
  input  [2:0] SEL,
  input  WE,
  output Aoe,
  output Awe,
  output [7:0] DataOut,
  output [15:0] AddrBus
);

  wire decoder_1_out1, decoder_1_out2, decoder_1_out3, decoder_1_out4, decoder_1_out5, decoder_1_out6,
       decoder_2_out1, decoder_2_out2, decoder_2_out3, decoder_2_out4, decoder_2_out5, decoder_2_out6;

  Decoder #(.select(3)) decoder_1 (
    .out0(Aoe), .out1(decoder_1_out1), .out2(decoder_1_out2), .out3(decoder_1_out3), .out4(decoder_1_out4),
    .out5(decoder_1_out5), .out6(decoder_1_out6), .sel(SEL), .en(OE));  // open: out7
  Decoder #(.select(3)) decoder_2 (
    .out0(Awe), .out1(decoder_2_out1), .out2(decoder_2_out2), .out3(decoder_2_out3), .out4(decoder_2_out4),
    .out5(decoder_2_out5), .out6(decoder_2_out6), .sel(SEL), .en(WE));  // open: out7
  regs B (.Din(Datain), .WE(decoder_2_out1), .Clck(Clk), .Rst(reset), .OE(decoder_1_out1), .Dout(DataOut));
  regs C (.Din(Datain), .WE(decoder_2_out2), .Clck(Clk), .Rst(reset), .OE(decoder_1_out2), .Dout(DataOut));
  regs D (.Din(Datain), .WE(decoder_2_out3), .Clck(Clk), .Rst(reset), .OE(decoder_1_out3), .Dout(DataOut));
  regs E (.Din(Datain), .WE(decoder_2_out4), .Clck(Clk), .Rst(reset), .OE(decoder_1_out4), .Dout(DataOut));
  HLreg hlreg_1 (
    .reset(reset), .DinH(Datain), .clock(Clk), .Hoe(decoder_1_out5), .Loe(decoder_1_out6), .DinL(Datain),
    .Hwe(decoder_2_out6), .Lwe(decoder_2_out5), .H_out(DataOut), .Dout(AddrBus), .L_out(DataOut));

  // Other names for the same wires on the sheet: rst = reset
endmodule

module PC (
  input  load,
  input  [15:0] AddrBusIn,
  input  PC_E,
  input  Clock,
  input  Clear,
  input  PC_OE,
  output [15:0] AddrBusOut
);

  wire [15:0] adder_1_out, multiplexer_1_out, register_1_q;

  Register #(.width(16)) register_1 (.D(multiplexer_1_out), .en(PC_E), .clk(Clock), .Q(register_1_q), .clr(Clear));
  Multiplexer #(.width(16)) multiplexer_1 (.in0(adder_1_out), .in1(AddrBusIn), .out(multiplexer_1_out), .sel(load));
  Multiplexer #(.width(16)) multiplexer_2 (.in0(16'h1), .in1({16{1'b1}}));  // open: out, sel
  Adder #(.width(16)) adder_1 (.a(register_1_q), .b(16'h1), .out(adder_1_out), .cin(1'b0));  // open: cout
  assign AddrBusOut = PC_OE ? register_1_q : 16'bz;  // Controlled_Buffer controlled_buffer_1

  // Notes on the sheet:
  //   if i am going to make stack pointer
endmodule

module CLK (
  input  butEnable,
  input  button,
  input  Halt,
  output Rise,
  output Fall,
  output FullClock
);

  wire and_1_out, clock_1_out, not_1_out, not_2_out, not_3_out, not_4_out, or_1_out;

  Clock clock_1 (.out(clock_1_out));
  and and_1 (and_1_out, butEnable, button);
  or or_1 (or_1_out, and_1_out, clock_1_out);
  and and_2 (FullClock, or_1_out, ~Halt);  // AND_Gate
  not not_1 (not_1_out, FullClock);
  and and_3 (Rise, FullClock, not_1_out);
  not not_2 (not_2_out, FullClock);
  not not_3 (not_3_out, FullClock);
  and and_4 (Fall, not_2_out, not_4_out);
  not not_4 (not_4_out, not_3_out);
endmodule

module HLreg (
  input  [7:0] DinH,
  input  Hoe,
  input  Hwe,
  input  Lwe,
  input  Loe,
  input  clock,
  input  reset,
  input  [7:0] DinL,
  output [7:0] H_out,
  output [15:0] Dout,
  output [7:0] L_out
);

  Register H (.D(DinH), .en(Hwe), .clk(clock), .Q(Dout[15:8]), .clr(reset));
  Register L (.D(DinL), .en(Lwe), .clk(clock), .Q(Dout[7:0]), .clr(reset));
  assign H_out = Hoe ? Dout[15:8] : 8'bz;  // Controlled_Buffer controlled_buffer_1
  assign L_out = Loe ? Dout[7:0] : 8'bz;  // Controlled_Buffer controlled_buffer_2
endmodule

module sequencer4step (
  input  resetState,
  input  clock,
  output out_3,
  output out_4,
  output out_5,
  output out_6
);

  wire d_ff_1_q, d_ff_1_qn, d_ff_2_q, d_ff_2_qn;

  D_Flip_Flop d_ff_1 (
    .D(d_ff_1_qn), .clk(clock), .Q(d_ff_1_q), .Qn(d_ff_1_qn), .preset(resetState), .reset(resetState));
  D_Flip_Flop d_ff_2 (
    .D(d_ff_2_qn), .clk(d_ff_1_q), .Q(d_ff_2_q), .Qn(d_ff_2_qn), .preset(resetState), .reset(resetState));
  and and_1 (out_4, d_ff_1_q, d_ff_2_q);
  and and_2 (out_5, d_ff_2_q, d_ff_1_qn);
  and and_3 (out_6, d_ff_1_q, d_ff_2_qn);
  and and_4 (out_3, d_ff_2_qn, d_ff_1_qn);
endmodule

module ALU2 (
  input  CEnbl,
  input  Cin,
  input  [7:0] A,
  input  [7:0] B,
  input  [2:0] OP,
  input  OutEn,
  output [7:0] out_7,
  output COut,
  output Z,
  output SaveFlag,
  output N,
  output V
);

  wire adder_1_cout, and_1_out, and_3_out, decoder_1_out0, decoder_1_out2, decoder_1_out3, decoder_1_out4,
       decoder_1_out5, nor_1_out, not_2_out, or_1_out, xor_2_out, xor_4_out, xor_5_out;
  wire [7:0] adder_1_out, and_2_out, controlled_buffer_1_out, not_1_out, or_2_out, xor_1_out, xor_3_out;
  wire [7:7] decoder_1_out1;

  // Probe on A
  // Probe on B
  assign xor_1_out = B ^ {8{decoder_1_out1[7]}};  // XOR_Gate xor_1, 8 bits wide
  Decoder #(.select(3)) decoder_1 (
    .out0(decoder_1_out0), .out1(decoder_1_out1[7]), .out2(decoder_1_out2), .out3(decoder_1_out3),
    .out4(decoder_1_out4), .out5(decoder_1_out5), .sel(OP), .en(1'b1));  // open: out6, out7
  and and_1 (and_1_out, CEnbl, Cin);
  xor xor_2 (xor_2_out, and_1_out, decoder_1_out1[7]);
  or or_1 (or_1_out, decoder_1_out1[7], decoder_1_out0);
  assign controlled_buffer_1_out = or_1_out ? adder_1_out : 8'bz;  // Controlled_Buffer controlled_buffer_1
  Adder adder_1 (.a(A), .b(xor_1_out), .out(adder_1_out), .cin(xor_2_out), .cout(adder_1_cout));
  assign and_2_out = A & xor_1_out;  // AND_Gate and_2, 8 bits wide
  assign controlled_buffer_1_out = decoder_1_out2 ? and_2_out : 8'bz;  // Controlled_Buffer controlled_buffer_2
  assign or_2_out = A | xor_1_out;  // OR_Gate or_2, 8 bits wide
  assign controlled_buffer_1_out = decoder_1_out3 ? or_2_out : 8'bz;  // Controlled_Buffer controlled_buffer_3
  assign xor_3_out = A ^ xor_1_out;  // XOR_Gate xor_3, 8 bits wide
  assign controlled_buffer_1_out = decoder_1_out4 ? xor_3_out : 8'bz;  // Controlled_Buffer controlled_buffer_4
  assign not_1_out = ~xor_1_out;  // NOT_Gate not_1, 8 bits wide
  assign controlled_buffer_1_out = decoder_1_out5 ? not_1_out : 8'bz;  // Controlled_Buffer controlled_buffer_5
  xor xor_4 (xor_4_out, controlled_buffer_1_out[7], A[7]);
  xor xor_5 (xor_5_out, A[7], B[7]);
  not not_2 (not_2_out, xor_5_out);
  nor nor_1 (nor_1_out, controlled_buffer_1_out[0], controlled_buffer_1_out[1], controlled_buffer_1_out[2], controlled_buffer_1_out[3], controlled_buffer_1_out[4], controlled_buffer_1_out[5], controlled_buffer_1_out[6], controlled_buffer_1_out[7]);
  and and_3 (and_3_out, xor_4_out, not_2_out);
  assign out_7 = OutEn ? controlled_buffer_1_out : 8'bz;  // Controlled_Buffer controlled_buffer_6
  assign COut = OutEn ? adder_1_cout : 1'bz;  // Controlled_Buffer controlled_buffer_7
  assign Z = OutEn ? nor_1_out : 1'bz;  // Controlled_Buffer controlled_buffer_8
  assign N = OutEn ? controlled_buffer_1_out[7] : 1'bz;  // Controlled_Buffer controlled_buffer_9
  assign V = OutEn ? and_3_out : 1'bz;  // Controlled_Buffer controlled_buffer_10
  // Probe on out_7

  assign SaveFlag = OutEn;
endmodule

module testt (
  input  in_1,
  input  in_2,
  input  in_3,
  input  in_4,
  input  in_5,
  input  in_6,
  output [7:0] out_7
);

  wire addrdecoder_1_erom, addrdecoder_1_ramoe, addrdecoder_1_ramwe, button_1_out, clck;
  wire [7:0] rom_1_data;
  wire [14:0] addrdecoder_1_addrout;
  wire [15:0] hlreg_1_dout, pc_1_addrbusout;

  Button button_1 (.out(button_1_out));
  CLK clk_1 (.butEnable(in_6), .button(button_1_out), .FullClock(clck));  // open: Halt, Rise, Fall
  PC pc_1 (.PC_E(in_3), .Clock(clck), .PC_OE(in_4), .AddrBusOut(pc_1_addrbusout));  // open: load, AddrBusIn, Clear
  HLreg hlreg_1 (.clock(clck), .Dout(hlreg_1_dout));  // open: reset, DinH, Hoe, Loe, DinL, Hwe, Lwe, H_out, L_out
  // Probe on pc_1_addrbusout
  addrDecoder addrdecoder_1 (
    .RAMwrite(in_1), .MEMread(in_2), .PC(pc_1_addrbusout), .HL(hlreg_1_dout), .eHL(in_5),
    .RAMwe(addrdecoder_1_ramwe), .RAMoe(addrdecoder_1_ramoe), .eROM(addrdecoder_1_erom),
    .addrOut(addrdecoder_1_addrout));  // open: imm, eIMM
  ROM #(.addrWidth(15)) rom_1 (.addr(addrdecoder_1_addrout), .data(rom_1_data));
  RAM #(.addrWidth(15), .databus("bidir")) ram_1 (
    .addr(addrdecoder_1_addrout), .we(addrdecoder_1_ramwe), .oe(addrdecoder_1_ramoe), .clk(clck), .data(out_7));
  assign out_7 = addrdecoder_1_erom ? rom_1_data : 8'bz;  // Controlled_Buffer controlled_buffer_1

  // Notes on the sheet:
  //   contents of rom_1 (hex, n*v repeats v):
  //   1 2 3 4 5 6 7 8 9 a b c d e f 10 11 12
endmodule

module Control (
  input  in_1,
  input  in_2
);

  // sequencer4step sequencer4step_1: pin names not known; wires that end beside it: in_1, in_2
endmodule

module addrDecoder (
  input  RAMwrite,
  input  MEMread,
  input  [15:0] PC,
  input  [15:0] HL,
  input  [15:0] imm,
  input  eHL,
  input  eIMM,
  output RAMwe,
  output RAMoe,
  output eROM,
  output [14:0] addrOut
);

  wire nor_1_out;
  wire [15:15] controlled_buffer_1_out;

  assign {controlled_buffer_1_out[15], addrOut} = nor_1_out ? PC : 16'bz;  // Controlled_Buffer controlled_buffer_1
  assign {controlled_buffer_1_out[15], addrOut} = eHL ? HL : 16'bz;  // Controlled_Buffer controlled_buffer_2
  nor nor_1 (nor_1_out, eHL, eIMM);
  Pull_Resistor pull_resistor_1 (.node({controlled_buffer_1_out[15], addrOut}));
  assign {controlled_buffer_1_out[15], addrOut} = eIMM ? imm : 16'bz;  // Controlled_Buffer controlled_buffer_3
  and and_1 (RAMwe, RAMwrite, controlled_buffer_1_out[15]);
  and and_2 (RAMoe, MEMread, controlled_buffer_1_out[15]);
  and and_3 (eROM, MEMread, ~controlled_buffer_1_out[15]);  // AND_Gate
  // Probe on addrOut

  // Notes on the sheet:
  //   0=ROM 1=RAM
endmodule

module CPU (
  input  in_1,
  input  [7:0] DATAtest
);

  wire alu_1_cout, FLAGflipflops_cout, undriven;
  wire [5:0] instrdecoder_1_add_op;
  wire [7:0] ACCUMULATOR_dout, controlled_buffer_1_out, INSTRUCTIONreg_out_5, rom_1_data, TEMP_dout;

  regs ACCUMULATOR (.Din(controlled_buffer_1_out), .Dout(ACCUMULATOR_dout));  // open: WE, Clck, Rst, OE
  // CLK clk_1: pin names not known
  regs TEMP (.Din(controlled_buffer_1_out), .Dout(TEMP_dout));  // open: WE, Clck, Rst, OE
  // PC pc_1: pin names not known
  assign controlled_buffer_1_out = in_1 ? DATAtest : 8'bz;  // Controlled_Buffer controlled_buffer_1
  flagReg FLAGflipflops (
    .Din(controlled_buffer_1_out), .Carryin(alu_1_cout), .WE(undriven), .Cout(FLAGflipflops_cout));  // open: Clck, Rst, Dout
  ALU alu_1 (
    .A(ACCUMULATOR_dout), .B(TEMP_dout), .in_6(instrdecoder_1_add_op), .Cin(FLAGflipflops_cout),
    .OutEn({1'bz, undriven}), .Dout(controlled_buffer_1_out), .COut(alu_1_cout));  // open: CEnbl
  instrReg INSTRUCTIONreg (.instIn(controlled_buffer_1_out), .out_5(INSTRUCTIONreg_out_5));  // open: WE, Clck, Rst
  instrDecoder instrdecoder_1 (
    .instr(INSTRUCTIONreg_out_5), .AND_op(instrdecoder_1_add_op[2]), .OR_op(instrdecoder_1_add_op[3]),
    .XOR_op(instrdecoder_1_add_op[4]), .NOT_op(instrdecoder_1_add_op[5]), .ADD_op(instrdecoder_1_add_op[0]),
    .SUB_op(instrdecoder_1_add_op[1]));  // open: HLT, ALUop, MemRegOp, REG_MUX, LW, SW, MOV, JMP, JZ, JC, NOP, CMP_op, HLuse
  // RegBank regbank_1: pin names not known
  // addrDecoder addrdecoder_1: pin names not known
  ROM #(.addrWidth(15)) rom_1 (.data(rom_1_data));  // open: addr
  RAM #(.addrWidth(15), .databus("bidir")) ram_1 ();  // open: addr, we, oe, clk, data
  Controlled_Buffer #(.width(8)) controlled_buffer_2 (.in(rom_1_data));  // open: out, en

  // Notes on the sheet:
  //   contents of rom_1 (hex, n*v repeats v):
  //   54
endmodule
